// Digital circuit ALU.dig as structural Verilog
module ALU (
  input  [7:0] A,
  input  [7:0] B,
  output [7:0] out
);

  wire [7:0] multiplexer_1_out, not_1_out, not_2_out;

  not not_1 (not_1_out[0], B[0]);
  not not_2 (not_2_out[0], A[0]);
  Multiplexer #(.Bits(8)) multiplexer_1 (.in_0(not_1_out), .in_1(B), .out(multiplexer_1_out));  // open: sel
  Multiplexer #(.Bits(8)) multiplexer_2 (.in_0(not_2_out), .in_1(A));  // open: sel, out
  // And and_1 has open pins: In_1=multiplexer_1_out[0], In_2=open, out=open
  // Pins of 1 and 8 bits meet at A
  // Pins of 1 and 8 bits meet at B
  // Pins of 1 and 8 bits meet at not_1_out
  // Pins of 1 and 8 bits meet at multiplexer_1_out
  // Pins of 1 and 8 bits meet at not_2_out
endmodule
