// Digital circuit CPUControlUnit.dig as structural Verilog
module CPUControlUnit (
  input  clock,
  input  control
);

  wire multiplexer_1_out;
  wire [5:0] MBR_q, MIR_q;

  CPUDataPath cpudatapath_1 ();  // open: z, n, c, o, ALU_Sel, MUX_Ctrl
  Register #(.Bits(6)) MIR (.Q(MIR_q));  // open: D, C, en
  Register #(.Bits(6)) MBR (.Q(MBR_q));  // open: D, C, en
  Multiplexer multiplexer_1 (.sel(control), .in_0(MIR_q[0]), .in_1(MBR_q[0]), .out(multiplexer_1_out));
  Register #(.Bits(6)) MPC (.C(clock), .en(multiplexer_1_out));  // open: D, Q
  ROM #(.AddrBits(6), .Bits(18)) rom_1 ();  // open: A, sel, D
  // Pins of 1 and 6 bits meet at MIR_q
  // Pins of 1 and 6 bits meet at MBR_q
endmodule
