// Digital circuit CPUDataPath.dig as structural Verilog
module CPUDataPath (
  input  [7:0] Input,
  input  Out_Wr,
  input  PC_Wr,
  input  MBR_Wr,
  input  B_Wr,
  input  A_Wr,
  input  [1:0] MUX_Ctrl,
  input  [3:0] ALU_Sel,
  input  clock,
  output z,
  output n,
  output c,
  output o
);

  wire [7:0] A_q, alu_1_out, B_q, MBR_q, multiplexer_1_out, OUT_q, PC_q;

  Register #(.Bits(8)) OUT (.D(alu_1_out), .C(clock), .en(Out_Wr), .Q(OUT_q));
  Register #(.Bits(8)) PC (.D(alu_1_out), .C(clock), .en(PC_Wr), .Q(PC_q));
  Register #(.Bits(8)) MBR (.D(alu_1_out), .C(clock), .en(MBR_Wr), .Q(MBR_q));
  Register #(.Bits(8)) B (.D(alu_1_out), .C(clock), .en(B_Wr), .Q(B_q));
  Register #(.Bits(8)) A (.D(alu_1_out), .C(clock), .en(A_Wr), .Q(A_q));
  Seven_Seg_Hex seven_seg_hex_1 (.d(OUT_q[3:0]), .dp(1'b0));
  Seven_Seg_Hex seven_seg_hex_2 (.d(OUT_q[7:4]), .dp(1'b0));
  Multiplexer #(.Selector_Bits(2), .Bits(8)) multiplexer_1 (
    .sel(MUX_Ctrl), .in_0(Input), .in_1(PC_q), .in_2(MBR_q), .in_3(B_q), .out(multiplexer_1_out));
  ALU alu_1 (
    .A(A_q), .B(multiplexer_1_out), .F0(ALU_Sel[3]), .F1(ALU_Sel[2]), .F2(ALU_Sel[1]), .F3(ALU_Sel[0]),
    .out(alu_1_out), .zero(z), .negative(n), .carry(c), .overflow(o));
endmodule
